# Fritzing sketch Attiny85 (saved by Fritzing 0.9.3b)
breadboards: 1

parts:
  U1 = attiny85 [package=dip]
  R1 = Resistor [tolerance=±5% resistance=1k package="0402 [SMD]"]
  LED1 = LED - 5mm [color="Red (633nm)" package="5 mm [THT]"]
  R2 = Resistor [tolerance=±5% resistance=1k package="0402 [SMD]"]
  D1 = Zener Diode [part_number=1N4732A breakdown_voltage=3.6V package="Melf DO-213 AB [SMD]"]
  HC-SR04_Sensor_1 = HC-SR04 Ultrasonic Distance Sensor
  J1 = Basic Servo

nets:
  N1: U1.Pin_2, R2.Pin_1, D1.cathode, HC-SR04_Sensor_1.TRIG
  N2: U1.Pin_3, J1.pulse
  N3: U1.Pin_4, LED1.cathode, D1.anode
  N4: U1.Pin_6, R1.Pin_1
  N5: R1.Pin_0, LED1.anode
  N6: R2.Pin_0, HC-SR04_Sensor_1.ECHO

notes:
  SCL
  SDA
  Ground
  5 volt
  3.3 Volts
