# Fritzing sketch SonarScope (saved by Fritzing 0.9.2b)
breadboards: 1

parts:
  Part1 = Pro Trinket 3.3V
  JACK1 = 2.1mm Barrel Jack with Terminal Block
  Raspberry_Pi1 = Raspberry Pi 2
  Part2 = HC-SR04 Ultrasonic Rangemeter
  J1 = Basic Servo
  R1 = Resistor [tolerance=±5% resistance=2.2k package="2010 [SMD]"]
  R2 = Resistor [tolerance=±5% resistance=1k package="2010 [SMD]"]

nets:
  GND: Part1.GND, JACK1.NEG, Raspberry_Pi1.GND, Part2.GND, J1.gnd, R1.Pin_0
  N1: Part1.VBAT, Raspberry_Pi1.3v3
  N2: Part1.D8, J1.pulse
  N3: Part1.A4, Raspberry_Pi1.GPIO2
  N4: Part1.A5, Raspberry_Pi1.GPIO3
  N5: JACK1.POS, J1.vcc
  N6: Raspberry_Pi1.GPIO22, R1.Pin_1, R2.Pin_1
  N7: Raspberry_Pi1.GPIO12, Part2.Trig
  5V: Raspberry_Pi1.5V, Part2.VCC
  N8: Part2.Echo, R2.Pin_0

custom parts:
  Pro Trinket 3.3V: The Pro Trinket 3.3V is like an Arduino Pro Mini with more pins and USB included. However, it uses 3V logic and 12MHz clock which means it's good when you want a lower-power and lower-voltage setup. Built with the common core Arduino chip, the ATmega328p, it has 18 GPIO, 2 extra analog inputs, 28K of flash, and 2K of RAM. It has onboard USB bootloading support with Optiboot support, so you can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
